# Fritzing sketch aquarium (saved by Fritzing 0.9.0b)
circuit board: 8.46667cm x 5.64444cm
breadboards: 1

parts:
  Tiny_RTC = Tiny RTC
  LCD1 = LCD screen
  R1 = Resistor [tolerance=±5% resistance=220 package=THT]
  Arduino_UNO = Arduino Uno (Rev3)
  R2 = Trimmer Potentiometer [maximum_resistance=10kΩ package=THT]
  S5 = Pushbutton [package="[THT]"]
  S4 = Pushbutton [package="[THT]"]
  S3 = Pushbutton [package="[THT]"]
  S2 = Pushbutton [package="[THT]"]
  S1 = Pushbutton [package="[THT]"]
  R7 = Resistor [tolerance=±5% resistance=2.2k package=THT]
  R6 = Resistor [tolerance=±5% resistance=1k package=THT]
  R5 = Resistor [tolerance=±5% resistance=680 package=THT]
  R4 = Resistor [tolerance=±5% resistance=330 package=THT]
  R3 = Resistor [tolerance=±5% resistance=2k package=THT]
  LED2 = LED - 5mm [color="Red (633nm)" package="5 mm [THT]"]
  LED3 = LED - 5mm [color="Yellow (585nm)" package="5 mm [THT]"]
  LED4 = LED - 5mm [color="Green (555nm)" package="5 mm [THT]"]
  LED5 = LED - 5mm [color="Blue (470nm)" package="5 mm [THT]"]
  R11 = Resistor [tolerance=±5% resistance=1k package=THT]
  R12 = Resistor [tolerance=±5% resistance=1k package=THT]
  R13 = Resistor [tolerance=±5% resistance=1k package=THT]
  R14 = Resistor [tolerance=±5% resistance=1k package=THT]
  LED1 = LED - 5mm [color="Green (570nm)" package="5 mm [THT]"]
  R15 = Resistor [tolerance=±5% resistance=1k package=THT]
  LED6 = RGB LED (com. cathode, rgb) [package="5 mm [THT]"]

nets:
  N1: Tiny_RTC.SCL, Arduino_UNO.A5/SCL
  N2: Tiny_RTC.SDA, Arduino_UNO.A4/SDA
  VCC: Tiny_RTC.VCC, LCD1.VDD, R1.Pin_0, Arduino_UNO.AREF, Arduino_UNO.5V, R2.leg2, R3.Pin_0, LED6.red_anode
  GND: Tiny_RTC.GND, LCD1.VSS, LCD1.R/W, LCD1.LED-, Arduino_UNO.GND, R2.leg1, S5.Pin_1, S5.Pin_2, S4.Pin_1, S4.Pin_2, S3.Pin_1, S3.Pin_2, S2.Pin_1, S2.Pin_2, S1.Pin_1, S1.Pin_2, R11.Pin_0, R12.Pin_0, R13.Pin_0, R14.Pin_0, R15.Pin_0, LED6.blue_anode
  N3: LCD1.V0, R2.wiper
  N4: LCD1.RS, Arduino_UNO.D13/SCK
  N5: LCD1.E, Arduino_UNO.D12/MISO
  N6: LCD1.DB4, Arduino_UNO.D5_PWM
  N7: LCD1.DB5, Arduino_UNO.D4
  N8: LCD1.DB6, Arduino_UNO.D3_PWM
  N9: LCD1.DB7, Arduino_UNO.D2
  N10: LCD1.LED+, R1.Pin_1
  N11: Arduino_UNO.A0, LED6.common_cathode
  N12: Arduino_UNO.A1, S1.Pin_3, S1.Pin_4, R4.Pin_0, R3.Pin_1
  N13: Arduino_UNO.D8, LED5.anode
  N14: Arduino_UNO.D9_PWM, LED4.anode
  N15: Arduino_UNO.D10_PWM/SS, LED3.anode
  N16: Arduino_UNO.D11_PWM/MOSI, LED2.anode
  N17: Arduino_UNO.D7, LED1.anode
  N18: S5.Pin_3, S5.Pin_4, R7.Pin_1
  N19: S4.Pin_3, S4.Pin_4, R7.Pin_0, R6.Pin_1
  N20: S3.Pin_3, S3.Pin_4, R6.Pin_0, R5.Pin_1
  N21: S2.Pin_3, S2.Pin_4, R5.Pin_0, R4.Pin_1
  N22: LED2.cathode, R11.Pin_1
  N23: LED3.cathode, R12.Pin_1
  N24: LED4.cathode, R13.Pin_1
  N25: LED5.cathode, R14.Pin_1
  N26: LED1.cathode, R15.Pin_1

custom parts:
  Tiny RTC: Tiny RTC I2C module DS1370Z RTC and AT24C32 EEPROM
